// Logisim project s-mips.circ as structural Verilog: 20 circuits, main circuit S-MIPS Board
module S_MIPS_Board (
  input  DESHABILITAR_DISPATCHER,
  output halt
);

  wire button_1_out, CLK, CS, d_ff_1_q, LCLR, LoadRAM, LoadRAMOn, LW, R_R_W, R_W, ram_dispatcher_1_finished,
       RCS, Reset_out, RST, TTY_EN;
  wire [2:0] KDB;
  wire [3:0] LMask, Mask, ram_1_read_time, ram_1_write_time, RMask;
  wire [6:0] KDB_DATA, TTY_DATA;
  wire [15:0] Addr, LAddr, RAddr;
  wire [31:0] I0, I1, I2, I3, LData, ram_1_data_out_0, ram_1_data_out_1, ram_1_data_out_2, ram_1_data_out_3,
       RI0, RI1, RI2, RI3;

  TTY #(.rows(25), .cols(80)) tty_1 (.data(TTY_DATA), .clk(CLK), .we(TTY_EN), .clr(RST));
  not not_1 (LoadRAMOn, ram_dispatcher_1_finished);
  RAM_Dispatcher ram_dispatcher_1 (
    .WriteTime(ram_1_write_time), .Clock(CLK), .Data(LData), .Address(LAddr), .Mask(LMask),
    .Finished(ram_dispatcher_1_finished), .Write(LW), .CLR(LCLR));
  Keyboard #(.buflen(64)) keyboard_1 (.clk(CLK), .re(KDB[0]), .avail(KDB[2]), .data(KDB_DATA));  // open: clr
  RAM ram_1 (
    .Address(RAddr), .Data_Out_0(ram_1_data_out_0), .Data_Out_1(ram_1_data_out_1),
    .Data_Out_2(ram_1_data_out_2), .Data_Out_3(ram_1_data_out_3), .Data_In_0(RI0), .Data_In_1(RI1),
    .Data_In_2(RI2), .Data_In_3(RI3), .Mask(RMask), .nRead_Write(R_R_W), .Chip_Select(RCS),
    .Read_Time(ram_1_read_time), .Reset(button_1_out), .Write_Time(ram_1_write_time));
  Button button_1 (.out(button_1_out));
  D_Flip_Flop d_ff_1 (.clk(CLK), .D(1'b1), .Q(d_ff_1_q), .reset(Reset_out));  // open: Qn, preset, en
  Button Reset (.out(Reset_out));
  S_MIPS s_mips_1 (
    .Kbd_Enable(KDB[0]), .Address(Addr), .Kbd_Clear(KDB[1]), .Kbd_Available(KDB[2]), .RAM_In_0(I0),
    .Kbd_ASCII_Data(KDB_DATA), .RAM_In_1(I1), .TTY_Enable(TTY_EN), .RAM_In_2(I2), .RAM_In_3(I3),
    .TTY_ASCII_Data(TTY_DATA), .Reset(RST), .RAM_Out_0(ram_1_data_out_0), .Clock(CLK),
    .RAM_Out_1(ram_1_data_out_1), .Stop(halt), .RAM_Out_2(ram_1_data_out_2), .RAM_Out_3(ram_1_data_out_3),
    .Mask(Mask), .Read_Time(ram_1_read_time), .Write_Time(ram_1_write_time), .nRead_Write(R_W),
    .Chip_Select(CS));
  D_Flip_Flop d_ff_2 (.clk(CLK), .D(d_ff_1_q), .Qn(LCLR), .reset(Reset_out));  // open: Q, preset, en
  or or_1 (RST, LCLR, LoadRAM);
  Clock clock_1 (.out(CLK));
  Multiplexer #(.width(32), .enable("false")) multiplexer_1 (.in0(I0), .in1(LData), .out(RI0), .sel(LoadRAM));
  Multiplexer #(.width(32), .enable("false")) multiplexer_2 (.in0(I1), .in1(LData), .out(RI1), .sel(LoadRAM));
  Multiplexer #(.width(32), .enable("false")) multiplexer_3 (.in0(I2), .in1(LData), .out(RI2), .sel(LoadRAM));
  Multiplexer #(.width(32), .enable("false")) multiplexer_4 (.in0(I3), .in1(LData), .out(RI3), .sel(LoadRAM));
  and and_1 (LoadRAM, ~DESHABILITAR_DISPATCHER, LoadRAMOn);  // AND_Gate
  Multiplexer #(.width(16), .enable("false")) multiplexer_5 (.in0(Addr), .in1(LAddr), .out(RAddr), .sel(LoadRAM));
  Multiplexer #(.width(4), .enable("false")) multiplexer_6 (.in0(Mask), .in1(LMask), .out(RMask), .sel(LoadRAM));
  Multiplexer #(.enable("false")) multiplexer_7 (.in0(CS), .in1(LW), .out(RCS), .sel(LoadRAM));
  Multiplexer #(.enable("false")) multiplexer_8 (.in0(R_W), .in1(LW), .out(R_R_W), .sel(LoadRAM));

  // Notes on the sheet:
  //   NO MODIFICAR
  //   Keyboard
endmodule

module RAM (
  input  [15:0] Address,
  input  [31:0] Data_In_0,
  input  [31:0] Data_In_1,
  input  [31:0] Data_In_2,
  input  [31:0] Data_In_3,
  input  [3:0] Mask,
  input  nRead_Write,
  input  Chip_Select,
  input  Reset,
  output [31:0] Data_Out_0,
  output [31:0] Data_Out_1,
  output [31:0] Data_Out_2,
  output [31:0] Data_Out_3,
  output [3:0] Read_Time,
  output [3:0] Write_Time
);

  wire and_2_out, and_3_out, and_4_out, and_5_out, and_6_out, and_7_out, and_8_out, and_9_out, Changed, CLK,
       comparator_2_eq, comparator_3_eq, comparator_4_eq, comparator_5_eq, comparator_6_eq, Count,
       demultiplexer_3_out0, Idle, Idle_q, Load, Load0, Load1, nand_1_out, or_1_out, or_2_out, or_3_out,
       or_4_out, or_5_out, or_6_out, or_7_out, or_8_out, or_9_out, or_10_out, Proc_q, Update_Mem, Zero_Time;
  wire [3:0] counter_1_q, multiplexer_1_out, subtractor_1_out;
  wire [31:0] register_1_q, register_2_q, register_3_q, register_4_q, register_5_q;

  // Probe on 4'b0011
  // Probe on 4'b0010
  Multiplexer #(.width(4), .enable("false")) multiplexer_1 (
    .in0(4'b0011), .in1(4'b0010), .out(multiplexer_1_out), .sel(nRead_Write));
  or or_1 (or_1_out, Idle, Update_Mem);
  or or_2 (or_2_out, ~Chip_Select, Reset);  // OR_Gate
  Subtractor #(.width(4)) subtractor_1 (.a(multiplexer_1_out), .b(4'b0010), .out(subtractor_1_out));  // open: bin, bout
  Demultiplexer #(.enable("false")) demultiplexer_1 (.out0(Idle), .out1(Load0), .in(Idle_q), .sel(Changed));
  D_Flip_Flop u_Idle (.clk(CLK), .D(or_1_out), .Q(Idle_q), .preset(or_2_out));  // open: Qn, en, reset
  // Probe on counter_1_q
  Counter #(.width(4), .max('hf)) counter_1 (
    .load(Load), .D(subtractor_1_out), .count(Count), .Q(counter_1_q), .clk(CLK), .clr(or_3_out));  // open: carry
  or or_3 (or_3_out, ~Chip_Select, Reset);  // OR_Gate
  Comparator #(.width(4), .mode("unsigned")) comparator_1 (
    .a(4'b0000), .b(counter_1_q), .eq(Zero_Time));  // open: gt, lt
  or or_4 (or_4_out, Count, Load0, Load1);
  Register #(.width(32)) register_1 (.D(Data_In_0), .en(Chip_Select), .Q(register_1_q), .clk(CLK), .clr(or_5_out));
  or or_5 (or_5_out, ~Chip_Select, Reset);  // OR_Gate
  Register #(.width(32)) register_2 (.D(Data_In_1), .en(Chip_Select), .Q(register_2_q), .clk(CLK), .clr(or_6_out));
  or or_6 (or_6_out, ~Chip_Select, Reset);  // OR_Gate
  Register #(.width(32)) register_3 (.D(Data_In_2), .en(Chip_Select), .Q(register_3_q), .clk(CLK), .clr(or_7_out));
  or or_7 (or_7_out, ~Chip_Select, Reset);  // OR_Gate
  Register #(.width(32)) register_4 (.D(Data_In_3), .en(Chip_Select), .Q(register_4_q), .clk(CLK), .clr(or_8_out));
  or or_8 (or_8_out, ~Chip_Select, Reset);  // OR_Gate
  Register #(.width(32)) register_5 (
    .D({{11{1'b1}}, nRead_Write, Mask, Address}), .en(Chip_Select), .Q(register_5_q), .clk(CLK),
    .clr(or_9_out));
  or or_9 (or_9_out, ~Chip_Select, Reset);  // OR_Gate
  D_Flip_Flop Proc (.clk(CLK), .D(or_4_out), .Q(Proc_q), .reset(or_10_out));  // open: Qn, preset, en
  or or_10 (or_10_out, ~Chip_Select, Reset);  // OR_Gate
  Demultiplexer #(.enable("false")) demultiplexer_2 (
    .out0(Count), .out1(Update_Mem), .in(demultiplexer_3_out0), .sel(Zero_Time));
  Demultiplexer #(.enable("false")) demultiplexer_3 (
    .out0(demultiplexer_3_out0), .out1(Load1), .in(Proc_q), .sel(Changed));
  Clock clock_1 (.out(CLK));
  Comparator #(.width(32)) comparator_2 (.a(register_1_q), .b(Data_In_0), .eq(comparator_2_eq));  // open: gt, lt
  Comparator #(.width(32)) comparator_3 (.a(register_2_q), .b(Data_In_1), .eq(comparator_3_eq));  // open: gt, lt
  Comparator #(.width(32)) comparator_4 (.a(register_3_q), .b(Data_In_2), .eq(comparator_4_eq));  // open: gt, lt
  Comparator #(.width(32)) comparator_5 (.a(register_4_q), .b(Data_In_3), .eq(comparator_5_eq));  // open: gt, lt
  Comparator #(.width(32)) comparator_6 (
    .a(register_5_q), .b({{11{1'b1}}, nRead_Write, Mask, Address}), .eq(comparator_6_eq));  // open: gt, lt
  nand nand_1 (nand_1_out, comparator_6_eq, comparator_2_eq, comparator_3_eq, comparator_4_eq, comparator_5_eq);
  and and_1 (Changed, nand_1_out, Chip_Select);
  or or_11 (Load, Count, Load1, Load0);
  and and_2 (and_2_out, Mask[0], Update_Mem, nRead_Write);
  and and_3 (and_3_out, Mask[1], Update_Mem, nRead_Write);
  and and_4 (and_4_out, Mask[2], Update_Mem, nRead_Write);
  and and_5 (and_5_out, Mask[3], Update_Mem, nRead_Write);
  RAM_part #(.addrWidth(16), .dataWidth(32), .bus("separate")) ram_1 (
    .addr(Address), .din(Data_In_0), .data(Data_Out_0), .str(and_2_out), .sel(Chip_Select), .clk(CLK),
    .ld(and_6_out), .clr(Reset));
  and and_6 (and_6_out, ~nRead_Write, Idle);  // AND_Gate
  RAM_part #(.addrWidth(16), .dataWidth(32), .bus("separate")) ram_2 (
    .addr(Address), .din(Data_In_1), .data(Data_Out_1), .str(and_3_out), .sel(Chip_Select), .clk(CLK),
    .ld(and_7_out), .clr(Reset));
  and and_7 (and_7_out, ~nRead_Write, Idle);  // AND_Gate
  RAM_part #(.addrWidth(16), .dataWidth(32), .bus("separate")) ram_3 (
    .addr(Address), .din(Data_In_2), .data(Data_Out_2), .str(and_4_out), .sel(Chip_Select), .clk(CLK),
    .ld(and_8_out), .clr(Reset));
  and and_8 (and_8_out, ~nRead_Write, Idle);  // AND_Gate
  RAM_part #(.addrWidth(16), .dataWidth(32), .bus("separate")) ram_4 (
    .addr(Address), .din(Data_In_3), .data(Data_Out_3), .str(and_5_out), .sel(Chip_Select), .clk(CLK),
    .ld(and_9_out), .clr(Reset));
  and and_9 (and_9_out, ~nRead_Write, Idle);  // AND_Gate

  assign Read_Time = 4'b0011;
  assign Write_Time = 4'b0010;

  // Other names for the same wires on the sheet: M0 = Mask[0]; M1 = Mask[1]; M2 = Mask[2]; M3 = Mask[3];
  //   RW = nRead_Write; CLR = Reset; CS = Chip_Select; Load2 = Count

  // Notes on the sheet:
  //   NO MODIFICAR
  //   excepto quizás los valores RT y WT
  //   BANK0
  //   BANK1
  //   BANK2
  //   BANK3
endmodule

module S_MIPS (
  input  Kbd_Available,
  input  [6:0] Kbd_ASCII_Data,
  input  [31:0] RAM_Out_0,
  input  [31:0] RAM_Out_1,
  input  Reset,
  input  [31:0] RAM_Out_2,
  input  Clock,
  input  [31:0] RAM_Out_3,
  input  [3:0] Read_Time,
  input  [3:0] Write_Time,
  output Kbd_Enable,
  output [15:0] Address,
  output Kbd_Clear,
  output TTY_Enable,
  output [6:0] TTY_ASCII_Data,
  output Stop,
  output [31:0] RAM_In_0,
  output [31:0] RAM_In_1,
  output [31:0] RAM_In_2,
  output [31:0] RAM_In_3,
  output [3:0] Mask,
  output nRead_Write,
  output Chip_Select
);

  wire data_path_1_tty, HALT, LOADING_INST, PC, PC_ADDRESS, RAM_INST, RAM_READ, WRITE_RAM;
  wire [31:0] MEMORY, RAM_DATA, read_from_ram_1_ram_data;

  Read_from_RAM read_from_ram_1 (
    .BANK0(RAM_Out_0), .BANK1(RAM_Out_1), .BANK2(RAM_Out_2), .BANK3(RAM_Out_3), .MEMORY(MEMORY),
    .RAM_DATA(read_from_ram_1_ram_data));
  Write_to_RAM write_to_ram_1 (
    .ADDRESS(Address), .VALUE(RAM_DATA), .MASK(Mask), .INPUT0(RAM_In_0), .INPUT1(RAM_In_1),
    .INPUT2(RAM_In_2), .INPUT3(RAM_In_3), .MEMORY(MEMORY));
  Data_Path data_path_1 (
    .CLK(Clock), .RESET(Reset), .EN_PC(PC), .KEYBOARD(Kbd_ASCII_Data), .RAM_READ(RAM_READ),
    .LOADING_INST(LOADING_INST), .WRITE_RAM(WRITE_RAM), .MEMORY_INST(RAM_INST), .HALT(HALT), .MEMORY(MEMORY),
    .RAM_DATA(RAM_DATA), .INSTRUCTION(read_from_ram_1_ram_data), .TTY(data_path_1_tty), .KBD(Kbd_Enable),
    .TTY_DATA(TTY_ASCII_Data), .PC_ADDRESS(PC_ADDRESS));
  Control_Unit control_unit_1 (
    .CLK(Clock), .RESET(Reset), .R_TIME(Read_Time), .W_TIME(Write_Time), .WRITE(WRITE_RAM), .HALT(HALT),
    .RAM_INST(RAM_INST), .STOP(Stop), .CS(Chip_Select), .WRITE_2(nRead_Write), .RAM_READ(RAM_READ),
    .LOADING_INST(LOADING_INST), .PC(PC), .PC_ADDRESS(PC_ADDRESS));
  and and_1 (TTY_Enable, data_path_1_tty, PC);

  assign Kbd_Clear = Reset;

  // Other names for the same wires on the sheet: CLK = Clock; CS = Chip_Select; KBD_AVAIL = Kbd_Available;
  //   CLR = Reset; KBD_CLR = Reset; KBD_DATA[6:0] = Kbd_ASCII_Data; RAM_A[15:0] = Address;
  //   RAM_INPUT_0[31:0] = RAM_In_0; RAM_INPUT_1[31:0] = RAM_In_1; RAM_INPUT_2[31:0] = RAM_In_2;
  //   RAM_INPUT_3[31:0] = RAM_In_3; RAM_MASK[3:0] = Mask; RAM_OUTPUT_0[31:0] = RAM_Out_0;
  //   RAM_OUTPUT_1[31:0] = RAM_Out_1; RAM_OUTPUT_2[31:0] = RAM_Out_2; RAM_OUTPUT_3[31:0] = RAM_Out_3;
  //   RW = nRead_Write; TTY_DATA[6:0] = TTY_ASCII_Data

  // Notes on the sheet:
  //   RAM ADDRESS
  //   DATA FROM RAM
  //   DATA TO RAM
  //   DATA WRITE MASK
  //   RAM TIMING
  //   RAM CONTROL
  //   KEYBOARD
  //   TTY
  //   SEQUENCING
endmodule

module RAM_Dispatcher (
  input  [3:0] WriteTime,
  input  Clock,
  input  CLR,
  output [31:0] Data,
  output [15:0] Address,
  output [3:0] Mask,
  output Finished,
  output Write
);

  wire demultiplexer_2_out1, demultiplexer_3_out1, End, IDLE_q, IncAddr, Load, or_1_out, or_2_out, While_q,
       WriteEnd;
  wire [3:0] counter_1_q;
  wire [31:0] CurrentAddress_q;

  Counter #(.width(32), .max('hffffffff)) CurrentAddress (
    .count(IncAddr), .Q({CurrentAddress_q[31:18], Address, CurrentAddress_q[1:0]}), .clk(Clock), .clr(CLR));  // open: load, D, carry
  or or_1 (or_1_out, IncAddr, demultiplexer_3_out1, Finished);
  D_Flip_Flop IDLE (.clk(Clock), .D(or_1_out), .Q(IDLE_q), .preset(CLR));  // open: Qn, en, reset
  Demultiplexer #(.enable("false")) demultiplexer_1 (.out0(Load), .out1(Finished), .in(IDLE_q), .sel(End));
  D_Flip_Flop While (.clk(Clock), .D(or_2_out), .Q(While_q), .reset(CLR));  // open: Qn, preset, en
  or or_2 (or_2_out, Write, Load);
  RAM_part #(.addrWidth(18), .dataWidth(32)) ram_1 (
    .addr({Address, CurrentAddress_q[1:0]}), .data(Data), .clk(Clock));  // open: sel, ld, clr
  Demultiplexer #(.enable("false")) demultiplexer_2 (
    .out0(Write), .out1(demultiplexer_2_out1), .in(While_q), .sel(WriteEnd));
  Decoder #(.select(2)) decoder_1 (
    .out0(Mask[0]), .out1(Mask[1]), .out2(Mask[2]), .out3(Mask[3]), .sel(CurrentAddress_q[1:0]));  // open: en
  Demultiplexer #(.enable("false")) demultiplexer_3 (
    .out0(IncAddr), .out1(demultiplexer_3_out1), .in(demultiplexer_2_out1), .sel(End));
  Counter #(.width(4), .max('hf)) counter_1 (
    .load(Load), .D(WriteTime), .count(Write), .Q(counter_1_q), .clk(Clock));  // open: carry, clr
  Comparator #(.width(32)) comparator_1 (.a(Data), .b({32{1'b1}}), .eq(End));  // open: gt, lt
  Comparator #(.width(4)) comparator_2 (.a(4'b0000), .b(counter_1_q), .eq(WriteEnd));  // open: gt, lt

  // Other names for the same wires on the sheet: CLK = Clock; Count = Write; WT[3:0] = WriteTime
endmodule

module Control_Unit (
  input  CLK,
  input  RESET,
  input  [3:0] R_TIME,
  input  [3:0] W_TIME,
  input  WRITE,
  input  HALT,
  input  RAM_INST,
  output PC,
  output LOADING_INST,
  output STOP,
  output CS,
  output RAM_READ,
  output WRITE_2,
  output PC_ADDRESS
);

  wire CHIP1, CHIP2, demultiplexer_1_out1, demultiplexer_2_out0, demultiplexer_3_out0, demultiplexer_4_out0,
       demultiplexer_5_out0, IDLE_q, LOADING_q, or_2_out, or_3_out, or_4_out, or_7_out, RAM, RAM_READ_t,
       STOP_t, timer_1_out, timer_2_out, TIMER_RESET;
  wire [3:0] multiplexer_1_out;

  or or_1 (PC, demultiplexer_5_out0, RAM_READ_t);
  or or_2 (or_2_out, demultiplexer_5_out0, RAM_READ_t, demultiplexer_1_out1);
  or or_3 (or_3_out, demultiplexer_2_out0, RAM);
  Multiplexer #(.width(4), .enable("false")) multiplexer_1 (
    .in0(R_TIME), .in1(W_TIME), .out(multiplexer_1_out), .sel(WRITE));
  D_Flip_Flop IDLE (.clk(CLK), .D(or_2_out), .Q(IDLE_q), .preset(RESET));  // open: Qn, en, reset
  Demultiplexer #(.enable("false")) demultiplexer_1 (
    .out0(TIMER_RESET), .out1(demultiplexer_1_out1), .in(IDLE_q), .sel(RESET));
  Demultiplexer #(.enable("false")) demultiplexer_2 (
    .out0(demultiplexer_2_out0), .out1(RAM_READ), .in(CHIP2), .sel(timer_1_out));
  D_Flip_Flop RAM_WAITER (.clk(CLK), .D(or_3_out), .Q(CHIP2), .reset(RESET));  // open: Qn, preset, en
  Timer timer_1 (.START(1'b1), .OUT(timer_1_out), .TIME(multiplexer_1_out), .CLK(CLK), .RESET(RAM));
  or or_4 (or_4_out, demultiplexer_3_out0, TIMER_RESET);
  D_Flip_Flop LOADING___X2 (.clk(CLK), .D(RAM_READ), .Q(RAM_READ_t), .reset(RESET));  // open: Qn, preset, en
  or or_5 (PC_ADDRESS, CHIP1, TIMER_RESET, PC);
  Demultiplexer #(.enable("false")) demultiplexer_3 (
    .out0(demultiplexer_3_out0), .out1(LOADING_INST), .in(CHIP1), .sel(timer_2_out));
  D_Flip_Flop READ_WAITER (.clk(CLK), .D(or_4_out), .Q(CHIP1), .reset(RESET));  // open: Qn, preset, en
  Timer timer_2 (.START(1'b1), .OUT(timer_2_out), .TIME(R_TIME), .CLK(CLK), .RESET(TIMER_RESET));
  or or_6 (CS, CHIP1, CHIP2);
  and and_1 (WRITE_2, CHIP2, WRITE);
  Demultiplexer #(.enable("false")) demultiplexer_4 (
    .out0(demultiplexer_4_out0), .out1(STOP_t), .in(LOADING_q), .sel(HALT));
  D_Flip_Flop LOADING (.clk(CLK), .D(LOADING_INST), .Q(LOADING_q), .reset(RESET));  // open: Qn, preset, en
  D_Flip_Flop u_HALT (.clk(CLK), .D(or_7_out), .Q(STOP), .reset(RESET));  // open: Qn, preset, en
  or or_7 (or_7_out, STOP, STOP_t);
  Demultiplexer #(.enable("false")) demultiplexer_5 (
    .out0(demultiplexer_5_out0), .out1(RAM), .in(demultiplexer_4_out0), .sel(RAM_INST));

  // Other names for the same wires on the sheet: RAM_RESET = RAM

  // Notes on the sheet:
  //   Control Unit
endmodule

module Data_Path (
  input  CLK,
  input  RESET,
  input  EN_PC,
  input  [31:0] INSTRUCTION,
  input  [6:0] KEYBOARD,
  input  PC_ADDRESS,
  input  RAM_READ,
  input  LOADING_INST,
  output [31:0] MEMORY,
  output MEMORY_INST,
  output WRITE_RAM,
  output [6:0] TTY_DATA,
  output KBD,
  output [31:0] RAM_DATA,
  output TTY,
  output HALT
);

  wire ADD, ADDI, AND, and_1_out, and_2_out, ANDI, BEQ, BGTZ, BLEZ, BLTZ, BNE, DIV, DIVU, J, JR, LW, MFHI,
       MFLO, MULT, MULU, NOP, NOR, OR, or_1_out, or_2_out, or_3_out, or_4_out, or_5_out, or_7_out, or_8_out,
       ORI, POP, PUSH, RF_WRITE, RND, SF, SLT, SLTI, SLTIU, SLTU, SUB, SW, TYPE_I, XOR, XORI, ZF;
  wire [3:0] alu_encoder_1_alu_selector;
  wire [4:0] multiplexer_1_out, RD, RS, RT;
  wire [15:0] CONSTANT;
  wire [25:0] DESTINO_SALTO;
  wire [31:0] ALU_OUTPUT, BC_OUT, bit_extender_1_out, bit_extender_2_out, HIGH, LOW, multiplexer_2_out,
       multiplexer_3_out, PC, random_1_out, register_1_q, register_file_input_1_output, RT_t, SP;
  wire [31:7] RS_t;

  Random #(.width(32)) random_1 (.clk(CLK), .next(RND), .out(random_1_out));  // open: clr
  or or_1 (or_1_out, ADD, AND, ORI, SUB, OR);
  or or_2 (or_2_out, XORI, RND, NOR, MFHI, XOR, MFLO, ADDI, KBD);
  or or_3 (or_3_out, SLTI, SLT, SLTIU, SLTU, ANDI);
  Register #(.width(32)) register_1 (.D(INSTRUCTION), .en(LOADING_INST), .Q(register_1_q), .clk(CLK), .clr(RESET));
  or or_4 (or_4_out, or_1_out, or_2_out, or_3_out);
  and and_1 (and_1_out, EN_PC, or_4_out);
  or or_5 (or_5_out, LW, POP);
  and and_2 (and_2_out, or_5_out, RAM_READ);
  Instruction_Decoder instruction_decoder_1 (
    .Instruction(register_1_q), .Constante(CONSTANT), .Destino_Salto(DESTINO_SALTO), .NOP(NOP), .SLTU(SLTU),
    .SLTIU(SLTIU), .BNE(BNE), .HALT(HALT), .ADD(ADD), .AND(AND), .ANDI(ANDI), .BLEZ(BLEZ), .TTY(TTY),
    .SUB(SUB), .SLT(SLT), .ORI(ORI), .BGTZ(BGTZ), .RND(RND), .MULT(MULT), .OR(OR), .LW(LW), .BLTZ(BLTZ),
    .KBD(KBD), .MULU(MULU), .NOR(NOR), .SW(SW), .J(J), .DIV(DIV), .XOR(XOR), .POP(POP), .JR(JR), .DIVU(DIVU),
    .ADDI(ADDI), .PUSH(PUSH), .MFHI(MFHI), .SLT_2(SLT), .SLTI(SLTI), .BEQ(BEQ), .MFLO(MFLO), .XORI(XORI),
    .RS(RS), .RT(RT), .RD(RD));
  Register_File_Input register_file_input_1 (
    .KEYBOARD(KEYBOARD), .ALU(ALU_OUTPUT), .RND(random_1_out), .MEMORY(INSTRUCTION), .HIGH(HIGH), .LOW(LOW),
    .LW(LW), .POP(POP), .MFHI(MFHI), .MFLO(MFLO), .isKBD(KBD), .isRND(RND),
    .Output(register_file_input_1_output));
  or or_6 (RF_WRITE, and_1_out, and_2_out);
  Multiplexer #(.width(5), .enable("false")) multiplexer_1 (.in0(RD), .in1(RT), .out(multiplexer_1_out), .sel(TYPE_I));
  or or_7 (or_7_out, LW, ADDI, SW);
  assign bit_extender_1_out = {{16{CONSTANT[15]}}, CONSTANT};  // Bit_Extender bit_extender_1
  Multiplexer #(.width(32), .enable("false")) multiplexer_2 (
    .in0(bit_extender_1_out), .in1(bit_extender_2_out), .out(multiplexer_2_out), .sel(or_8_out));
  assign bit_extender_2_out = {{16{1'b0}}, CONSTANT};  // Bit_Extender bit_extender_2
  or or_8 (or_8_out, ANDI, XORI, ORI);
  Register_File register_file_1 (
    .RESET(RESET), .PUSH(PUSH), .CLK(CLK), .POP(POP), .INPUT(register_file_input_1_output), .WRITE(RF_WRITE),
    .SelOutA(RS), .SELECTOR(multiplexer_1_out), .SelOutB(RT), .OutA({RS_t, TTY_DATA}), .Out31(SP),
    .OutB(RT_t), .EN_PC(EN_PC));
  Memory_Address memory_address_1 (
    .ALU(ALU_OUTPUT), .PC(PC), .SP(SP), .POP(POP), .PUSH(PUSH), .LW(LW), .SW(SW), .PC_ADDRESS(PC_ADDRESS),
    .MEMORY(MEMORY));
  Multiplexer #(.width(32), .enable("false")) multiplexer_3 (
    .in0(RT_t), .in1(multiplexer_2_out), .out(multiplexer_3_out), .sel(TYPE_I));
  ALU_Encoder alu_encoder_1 (
    .ADD(ADD), .ADDI(or_7_out), .SUB(SUB), .MULT(MULT), .MULU(MULU), .DIV(DIV), .DIVU(DIVU), .SLT(SLT),
    .SLTI(SLTI), .OR(OR), .SLTU(SLTU), .ORI(ORI), .SLTIU(SLTIU), .XOR(XOR), .AND(AND), .XORI(XORI),
    .ANDI(ANDI), .NOR(NOR), .ALU_SELECTOR(alu_encoder_1_alu_selector), .TYPE_I(TYPE_I));
  or or_9 (WRITE_RAM, SW, PUSH);
  Multiplexer #(.width(32), .enable("false")) multiplexer_4 (
    .in0({RS_t, TTY_DATA}), .in1(RT_t), .out(RAM_DATA), .sel(SW));
  ALU alu_1 (
    .ALU_Selector(alu_encoder_1_alu_selector), .X({RS_t, TTY_DATA}), .CLK(CLK), .Y(multiplexer_3_out),
    .HIGH(HIGH), .ALU_OUTPUT(ALU_OUTPUT), .LOW(LOW), .ZF(ZF), .SF(SF));
  or or_10 (MEMORY_INST, LW, WRITE_RAM, POP);
  Program_Counter program_counter_1 (.ENABLE(EN_PC), .PC_OUTPUT(PC), .RESET(RESET), .INPUT(BC_OUT), .CLK(CLK));
  Branch_Control branch_control_1 (
    .BEQ(BEQ), .BNE(BNE), .BLEZ(BLEZ), .BGTZ(BGTZ), .BLTZ(BLTZ), .JR(JR), .J(J), .DEST(DESTINO_SALTO),
    .RS({RS_t, TTY_DATA}), .RT(RT_t), .PC(PC), .CONST(CONSTANT), .BC_OUT(BC_OUT));

  // Other names for the same wires on the sheet: RS_t[6:0] = TTY_DATA

  // Notes on the sheet:
  //   Data Path
endmodule

module ALU (
  input  [3:0] ALU_Selector,
  input  CLK,
  input  [31:0] X,
  input  [31:0] Y,
  output [31:0] ALU_OUTPUT,
  output [31:0] HIGH,
  output ZF,
  output SF,
  output [31:0] LOW
);

  wire comparator_1_lt, comparator_2_lt, ENABLE_HIGH_LOW;
  wire [1:0] SELECTOR_MUL_DIV;
  wire [31:0] ADD, AND, DIV_highoutput, DIV_lowoutput, divider_1_out, divider_1_rem, multiplexer_2_out,
       multiplexer_3_out, multiplier_1_cout, multiplier_1_out, MULU_highoutput, MULU_lowoutput, NOR, OR, SLT,
       SLTU, SUB, XOR;

  assign AND = X & Y;  // AND_Gate and_1, 32 bits wide
  assign OR = X | Y;  // OR_Gate or_1, 32 bits wide
  assign NOR = ~(X | Y);  // NOR_Gate nor_1, 32 bits wide
  assign XOR = X ^ Y;  // XOR_Gate xor_1, 32 bits wide
  Comparator #(.width(32)) comparator_1 (.a(X), .b(Y), .lt(comparator_1_lt));  // open: gt, eq
  assign SLT = {{31{1'b0}}, comparator_1_lt};  // Bit_Extender bit_extender_1
  Comparator #(.width(32), .mode("unsigned")) comparator_2 (.a(X), .b(Y), .lt(comparator_2_lt));  // open: gt, eq
  assign SLTU = {{31{1'b0}}, comparator_2_lt};  // Bit_Extender bit_extender_2
  Adder #(.width(32)) adder_1 (.a(X), .b(Y), .out(ADD));  // open: cin, cout
  Subtractor #(.width(32)) subtractor_1 (.a(X), .b(Y), .out(SUB));  // open: bin, bout
  Multiplier #(.width(32)) multiplier_1 (.a(X), .b(Y), .out(multiplier_1_out), .cout(multiplier_1_cout));  // open: cin
  Divider #(.width(32)) divider_1 (.a(X), .b(Y), .out(divider_1_out), .rem(divider_1_rem));  // open: upper
  Signed_Divider DIV (.A(X), .B(Y), .LowOutput(DIV_lowoutput), .HighOutput(DIV_highoutput));
  Unsigned_Multiplier MULU (.A(X), .B(Y), .LowOutput(MULU_lowoutput), .HighOutput(MULU_highoutput));
  Multiplexer #(.select(4), .width(32), .enable("false")) multiplexer_1 (
    .in0(AND), .in1(OR), .in2(NOR), .in3(XOR), .in4(SLT), .in5(SLTU), .in6(ADD), .in7(SUB), .out(ALU_OUTPUT),
    .sel(ALU_Selector));  // open: in8, in9, in10, in11, in12, in13, in14, in15
  Multiplexer #(.select(2), .width(32), .enable("false")) multiplexer_2 (
    .in0(multiplier_1_cout), .in1(divider_1_rem), .in2(DIV_highoutput), .in3(MULU_highoutput),
    .out(multiplexer_2_out), .sel(SELECTOR_MUL_DIV));
  Multiplexer #(.select(2), .width(32), .enable("false")) multiplexer_3 (
    .in0(multiplier_1_out), .in1(divider_1_out), .in2(DIV_lowoutput), .in3(MULU_lowoutput),
    .out(multiplexer_3_out), .sel(SELECTOR_MUL_DIV));
  Comparator #(.width(32)) comparator_3 (.a(ALU_OUTPUT), .b({32{1'b1}}), .eq(ZF), .lt(SF));  // open: gt
  and and_2 (ENABLE_HIGH_LOW, ALU_Selector[3], ~ALU_Selector[2]);  // AND_Gate
  and and_3 (SELECTOR_MUL_DIV[1], ALU_Selector[3], ~ALU_Selector[2], ALU_Selector[1]);  // AND_Gate
  and and_4 (SELECTOR_MUL_DIV[0], ALU_Selector[3], ~ALU_Selector[2], ALU_Selector[0]);  // AND_Gate
  Register #(.width(32)) register_1 (.D(multiplexer_2_out), .en(ENABLE_HIGH_LOW), .Q(HIGH), .clk(CLK));  // open: clr
  Register #(.width(32)) register_2 (.D(multiplexer_3_out), .en(ENABLE_HIGH_LOW), .Q(LOW), .clk(CLK));  // open: clr

  // Notes on the sheet:
  //   ALU
endmodule

module ALU_Encoder (
  input  ADD,
  input  ADDI,
  input  SUB,
  input  MULT,
  input  MULU,
  input  DIV,
  input  DIVU,
  input  SLT,
  input  SLTI,
  input  SLTU,
  input  SLTIU,
  input  AND,
  input  ANDI,
  input  OR,
  input  ORI,
  input  XOR,
  input  XORI,
  input  NOR,
  output TYPE_I,
  output [3:0] ALU_SELECTOR
);

  wire ADD_t, AND_t, OR_t, SLT_t, SLTU_t, XOR_t;

  or or_1 (ADD_t, ADD, ADDI);
  or or_2 (SLT_t, SLT, SLTI);
  or or_3 (SLTU_t, SLTU, SLTIU);
  or or_4 (AND_t, AND, ANDI);
  or or_5 (OR_t, OR, ORI);
  or or_6 (XOR_t, XOR, XORI);
  or or_7 (TYPE_I, ADDI, SLTI, SLTIU, ANDI, ORI, XORI);
  or or_8 (ALU_SELECTOR[3], MULT, DIVU, DIV, MULU);
  or or_9 (ALU_SELECTOR[2], SLT_t, SLTU_t, ADD_t, SUB);
  or or_10 (ALU_SELECTOR[1], NOR, XOR_t, ADD_t, SUB, DIV, MULU);
  or or_11 (ALU_SELECTOR[0], OR_t, XOR_t, SLTU_t, SUB, DIVU, MULU);

  // Notes on the sheet:
  //   ALU_Encoder
endmodule

module Register_File (
  input  RESET,
  input  PUSH,
  input  CLK,
  input  POP,
  input  [31:0] INPUT,
  input  WRITE,
  input  [4:0] SelOutA,
  input  [4:0] SELECTOR,
  input  [4:0] SelOutB,
  input  EN_PC,
  output [31:0] OutA,
  output [31:0] Out31,
  output [31:0] OutB
);

  wire In31, L0, L1, L2, L3, L4, L5, L6, L7, L8, L9, L10, L11, L12, L13, L14, L15, L16, L17, L18, L19, L20,
       L21, L22, L23, L24, L25, L26, L27, L28, L29, L30, L31, or_1_out, or_2_out;
  wire [31:0] adder_1_out, multiplexer_2_out, multiplexer_3_out, multiplexer_4_out, Out0, Out1, Out2, Out3,
       Out4, Out5, Out6, Out7, Out8, Out9, Out10, Out11, Out12, Out13, Out14, Out15, Out16, Out17, Out18,
       Out19, Out20, Out21, Out22, Out23, Out24, Out25, Out26, Out27, Out28, Out29, Out30, subtractor_1_out;

  Demultiplexer #(.select(5), .enable("false")) demultiplexer_1 (
    .out0(L0), .out1(L1), .out2(L2), .out3(L3), .out4(L4), .out5(L5), .out6(L6), .out7(L7), .out8(L8),
    .out9(L9), .out10(L10), .out11(L11), .out12(L12), .out13(L13), .out14(L14), .out15(L15), .out16(L16),
    .out17(L17), .out18(L18), .out19(L19), .out20(L20), .out21(L21), .out22(L22), .out23(L23), .out24(L24),
    .out25(L25), .out26(L26), .out27(L27), .out28(L28), .out29(L29), .out30(L30), .out31(In31), .in(WRITE),
    .sel(SELECTOR));
  Register #(.width(32)) R0 (.D({32{1'b0}}), .en(L0), .Q(Out0), .clk(CLK), .clr(RESET));
  Register #(.width(32)) R8 (.D(INPUT), .en(L8), .Q(Out8), .clk(CLK), .clr(RESET));
  Register #(.width(32)) R16 (.D(INPUT), .en(L16), .Q(Out16), .clk(CLK), .clr(RESET));
  Register #(.width(32)) R24 (.D(INPUT), .en(L24), .Q(Out24), .clk(CLK), .clr(RESET));
  Register #(.width(32)) R1 (.D(INPUT), .en(L1), .Q(Out1), .clk(CLK), .clr(RESET));
  Register #(.width(32)) R9 (.D(INPUT), .en(L9), .Q(Out9), .clk(CLK), .clr(RESET));
  Register #(.width(32)) R17 (.D(INPUT), .en(L17), .Q(Out17), .clk(CLK), .clr(RESET));
  Register #(.width(32)) R25 (.D(INPUT), .en(L25), .Q(Out25), .clk(CLK), .clr(RESET));
  Register #(.width(32)) R2 (.D(INPUT), .en(L2), .Q(Out2), .clk(CLK), .clr(RESET));
  Register #(.width(32)) R10 (.D(INPUT), .en(L10), .Q(Out10), .clk(CLK), .clr(RESET));
  Register #(.width(32)) R18 (.D(INPUT), .en(L18), .Q(Out18), .clk(CLK), .clr(RESET));
  Register #(.width(32)) R26 (.D(INPUT), .en(L26), .Q(Out26), .clk(CLK), .clr(RESET));
  Register #(.width(32)) R3 (.D(INPUT), .en(L3), .Q(Out3), .clk(CLK), .clr(RESET));
  Register #(.width(32)) R11 (.D(INPUT), .en(L11), .Q(Out11), .clk(CLK), .clr(RESET));
  Register #(.width(32)) R19 (.D(INPUT), .en(L19), .Q(Out19), .clk(CLK), .clr(RESET));
  Register #(.width(32)) R27 (.D(INPUT), .en(L27), .Q(Out27), .clk(CLK), .clr(RESET));
  Register #(.width(32)) R4 (.D(INPUT), .en(L4), .Q(Out4), .clk(CLK), .clr(RESET));
  Register #(.width(32)) R12 (.D(INPUT), .en(L12), .Q(Out12), .clk(CLK), .clr(RESET));
  Register #(.width(32)) R20 (.D(INPUT), .en(L20), .Q(Out20), .clk(CLK), .clr(RESET));
  Register #(.width(32)) R28 (.D(INPUT), .en(L28), .Q(Out28), .clk(CLK), .clr(RESET));
  Register #(.width(32)) R5 (.D(INPUT), .en(L5), .Q(Out5), .clk(CLK), .clr(RESET));
  Register #(.width(32)) R13 (.D(INPUT), .en(L13), .Q(Out13), .clk(CLK), .clr(RESET));
  Register #(.width(32)) R21 (.D(INPUT), .en(L21), .Q(Out21), .clk(CLK), .clr(RESET));
  Register #(.width(32)) R29 (.D(INPUT), .en(L29), .Q(Out29), .clk(CLK), .clr(RESET));
  Register #(.width(32)) R6 (.D(INPUT), .en(L6), .Q(Out6), .clk(CLK), .clr(RESET));
  Register #(.width(32)) R14 (.D(INPUT), .en(L14), .Q(Out14), .clk(CLK), .clr(RESET));
  Register #(.width(32)) R22 (.D(INPUT), .en(L22), .Q(Out22), .clk(CLK), .clr(RESET));
  Register #(.width(32)) R30 (.D(INPUT), .en(L30), .Q(Out30), .clk(CLK), .clr(RESET));
  Multiplexer #(.select(5), .width(32), .enable("false")) multiplexer_1 (
    .in0(Out0), .in1(Out1), .in2(Out2), .in3(Out3), .in4(Out4), .in5(Out5), .in6(Out6), .in7(Out7),
    .in8(Out8), .in9(Out9), .in10(Out10), .in11(Out11), .in12(Out12), .in13(Out13), .in14(Out14),
    .in15(Out15), .in16(Out16), .in17(Out17), .in18(Out18), .in19(Out19), .in20(Out20), .in21(Out21),
    .in22(Out22), .in23(Out23), .in24(Out24), .in25(Out25), .in26(Out26), .in27(Out27), .in28(Out28),
    .in29(Out29), .in30(Out30), .in31(Out31), .out(OutA), .sel(SelOutA));
  Register #(.width(32)) R7 (.D(INPUT), .en(L7), .Q(Out7), .clk(CLK), .clr(RESET));
  Register #(.width(32)) R15 (.D(INPUT), .en(L15), .Q(Out15), .clk(CLK), .clr(RESET));
  Register #(.width(32)) R23 (.D(INPUT), .en(L23), .Q(Out23), .clk(CLK), .clr(RESET));
  Subtractor #(.width(32)) subtractor_1 (.a(Out31), .b(32'h4), .out(subtractor_1_out));  // open: bin, bout
  Multiplexer #(.width(32), .enable("false")) multiplexer_2 (
    .in0(subtractor_1_out), .in1(adder_1_out), .out(multiplexer_2_out), .sel(POP));
  Multiplexer #(.width(32), .enable("false")) multiplexer_3 (
    .in0(multiplexer_2_out), .in1({32{1'b1}}), .out(multiplexer_3_out), .sel(RESET));
  Multiplexer #(.width(32), .enable("false")) multiplexer_4 (
    .in0(multiplexer_3_out), .in1(INPUT), .out(multiplexer_4_out), .sel(In31));
  Register #(.width(32)) register_1 (.D(multiplexer_4_out), .en(or_1_out), .Q(Out31), .clk(CLK));  // open: clr
  or or_1 (or_1_out, RESET, In31, L31);
  Adder #(.width(32)) adder_1 (.a(Out31), .b(32'h4), .out(adder_1_out));  // open: cin, cout
  or or_2 (or_2_out, PUSH, POP);
  Multiplexer #(.select(5), .width(32), .enable("false")) multiplexer_5 (
    .in0(Out0), .in1(Out1), .in2(Out2), .in3(Out3), .in4(Out4), .in5(Out5), .in6(Out6), .in7(Out7),
    .in8(Out8), .in9(Out9), .in10(Out10), .in11(Out11), .in12(Out12), .in13(Out13), .in14(Out14),
    .in15(Out15), .in16(Out16), .in17(Out17), .in18(Out18), .in19(Out19), .in20(Out20), .in21(Out21),
    .in22(Out22), .in23(Out23), .in24(Out24), .in25(Out25), .in26(Out26), .in27(Out27), .in28(Out28),
    .in29(Out29), .in30(Out30), .in31(Out31), .out(OutB), .sel(SelOutB));
  and and_1 (L31, or_2_out, EN_PC);

  // Notes on the sheet:
  //   REGISTER FILE
endmodule

module Register_File_Input (
  input  [6:0] KEYBOARD,
  input  [31:0] ALU,
  input  [31:0] RND,
  input  [31:0] MEMORY,
  input  [31:0] HIGH,
  input  [31:0] LOW,
  input  LW,
  input  POP,
  input  MFHI,
  input  MFLO,
  input  isKBD,
  input  isRND,
  output [31:0] Output
);

  wire [2:0] SELECTOR;

  or or_1 (SELECTOR[2], MFLO, isKBD, isRND);
  or or_2 (SELECTOR[1], POP, MFHI, isRND);
  or or_3 (SELECTOR[0], LW, MFHI, isKBD);
  Multiplexer #(.select(3), .width(32), .enable("false")) multiplexer_1 (
    .in0(ALU), .in1(MEMORY), .in2(MEMORY), .in3(HIGH), .in4(LOW), .in5({{25{1'b0}}, KEYBOARD}), .in6(RND),
    .out(Output), .sel(SELECTOR));  // open: in7

  // Other names for the same wires on the sheet: KBD[6:0] = KEYBOARD

  // Notes on the sheet:
  //   Register File Input
endmodule

module Program_Counter (
  input  [31:0] INPUT,
  input  ENABLE,
  input  RESET,
  input  CLK,
  output [31:0] PC_OUTPUT
);

  Register #(.width(32)) register_1 (.D(INPUT), .en(ENABLE), .Q(PC_OUTPUT), .clk(CLK), .clr(RESET));

  // Notes on the sheet:
  //   PROGRAM COUNTER
endmodule

module Instruction_Decoder (
  input  [31:0] Instruction,
  output [15:0] Constante,
  output [25:0] Destino_Salto,
  output [4:0] RT,
  output [4:0] RS,
  output [4:0] RD,
  output NOP,
  output SLTU,
  output SLTIU,
  output BNE,
  output HALT,
  output ADD,
  output AND,
  output ANDI,
  output BLEZ,
  output TTY,
  output SUB,
  output SLT,
  output ORI,
  output BGTZ,
  output RND,
  output XORI,
  output MULT,
  output OR,
  output BLTZ,
  output KBD,
  output LW,
  output MULU,
  output NOR,
  output J,
  output SW,
  output DIV,
  output XOR,
  output JR,
  output POP,
  output DIVU,
  output ADDI,
  output MFHI,
  output PUSH,
  output SLT_2,
  output SLTI,
  output MFLO,
  output BEQ
);

  wire _000000, _111111, comparator_11_eq, comparator_11_gt, comparator_12_eq, comparator_19_eq,
       comparator_20_eq, comparator_21_eq, comparator_22_eq, comparator_23_eq, comparator_24_eq,
       comparator_25_eq, comparator_26_eq, comparator_27_eq, comparator_28_eq, comparator_29_eq,
       comparator_30_eq, comparator_31_eq, comparator_32_eq, comparator_33_eq, comparator_34_eq,
       comparator_35_eq, comparator_36_eq, comparator_37_eq, comparator_38_eq;

  Comparator #(.width(6)) comparator_1 (.a(Instruction[31:26]), .b({6{1'b0}}), .eq(_000000));  // open: gt, lt
  Comparator #(.width(6)) comparator_2 (.a(Instruction[31:26]), .b({6{1'b1}}), .eq(_111111));  // open: gt, lt
  Comparator #(.width(6)) comparator_3 (.a(Instruction[31:26]), .b(6'b001000), .eq(ADDI));  // open: gt, lt
  Comparator #(.width(6)) comparator_4 (.a(Instruction[31:26]), .b(6'b001010), .eq(SLTI));  // open: gt, lt
  Comparator #(.width(6)) comparator_5 (.a(Instruction[31:26]), .b(6'b001011), .eq(SLTIU));  // open: gt, lt
  Comparator #(.width(6)) comparator_6 (.a(Instruction[31:26]), .b(6'b001100), .eq(ANDI));  // open: gt, lt
  Comparator #(.width(6)) comparator_7 (.a(Instruction[31:26]), .b(6'b001101), .eq(ORI));  // open: gt, lt
  Comparator #(.width(6)) comparator_8 (.a(Instruction[31:26]), .b(6'b001110), .eq(XORI));  // open: gt, lt
  Comparator #(.width(6)) comparator_9 (.a(Instruction[31:26]), .b(6'b100011), .eq(LW));  // open: gt, lt
  Comparator #(.width(6)) comparator_10 (.a(Instruction[31:26]), .b(6'b101011), .eq(SW));  // open: gt, lt
  Comparator #(.width(6)) comparator_11 (
    .a(Instruction[5:0]), .b({6{1'b0}}), .gt(comparator_11_gt), .eq(comparator_11_eq));  // open: lt
  and and_1 (POP, comparator_11_eq, comparator_12_eq);
  Comparator #(.width(6)) comparator_12 (.a(Instruction[31:26]), .b(6'b111000), .eq(comparator_12_eq));  // open: gt, lt
  Comparator #(.width(6)) comparator_13 (.a(Instruction[31:26]), .b(6'b000100), .eq(BEQ));  // open: gt, lt
  Comparator #(.width(6)) comparator_14 (.a(Instruction[31:26]), .b(6'b000101), .eq(BNE));  // open: gt, lt
  Comparator #(.width(6)) comparator_15 (.a(Instruction[31:26]), .b(6'b000110), .eq(BLEZ));  // open: gt, lt
  Comparator #(.width(6)) comparator_16 (.a(Instruction[31:26]), .b(6'b000111), .eq(BGTZ));  // open: gt, lt
  Comparator #(.width(6)) comparator_17 (.a(Instruction[31:26]), .b(6'b000001), .eq(BLTZ));  // open: gt, lt
  Comparator #(.width(6)) comparator_18 (.a(Instruction[31:26]), .b(6'b000010), .eq(J));  // open: gt, lt
  and and_2 (PUSH, comparator_11_gt, comparator_12_eq);
  and and_3 (HALT, _111111, comparator_19_eq);
  Comparator #(.width(6)) comparator_19 (.a(Instruction[5:0]), .b({6{1'b1}}), .eq(comparator_19_eq));  // open: gt, lt
  and and_4 (TTY, _111111, comparator_20_eq);
  Comparator #(.width(6)) comparator_20 (.a(Instruction[5:0]), .b(6'b000001), .eq(comparator_20_eq));  // open: gt, lt
  and and_5 (RND, _111111, comparator_21_eq);
  Comparator #(.width(6)) comparator_21 (.a(Instruction[5:0]), .b(6'b000010), .eq(comparator_21_eq));  // open: gt, lt
  and and_6 (KBD, _111111, comparator_22_eq);
  Comparator #(.width(6)) comparator_22 (.a(Instruction[5:0]), .b(6'b000100), .eq(comparator_22_eq));  // open: gt, lt
  Comparator #(.width(6)) comparator_23 (.a(Instruction[5:0]), .b({6{1'b0}}), .eq(comparator_23_eq));  // open: gt, lt
  Comparator #(.width(6)) comparator_24 (.a(Instruction[5:0]), .b(6'b100000), .eq(comparator_24_eq));  // open: gt, lt
  Comparator #(.width(6)) comparator_25 (.a(Instruction[5:0]), .b(6'b100010), .eq(comparator_25_eq));  // open: gt, lt
  Comparator #(.width(6)) comparator_26 (.a(Instruction[5:0]), .b(6'b011000), .eq(comparator_26_eq));  // open: gt, lt
  Comparator #(.width(6)) comparator_27 (.a(Instruction[5:0]), .b(6'b011001), .eq(comparator_27_eq));  // open: gt, lt
  Comparator #(.width(6)) comparator_28 (.a(Instruction[5:0]), .b(6'b011010), .eq(comparator_28_eq));  // open: gt, lt
  Comparator #(.width(6)) comparator_29 (.a(Instruction[5:0]), .b(6'b011011), .eq(comparator_29_eq));  // open: gt, lt
  Comparator #(.width(6)) comparator_30 (.a(Instruction[5:0]), .b(6'b101010), .eq(comparator_30_eq));  // open: gt, lt
  Comparator #(.width(6)) comparator_31 (.a(Instruction[5:0]), .b(6'b101011), .eq(comparator_31_eq));  // open: gt, lt
  Comparator #(.width(6)) comparator_32 (.a(Instruction[5:0]), .b(6'b100100), .eq(comparator_32_eq));  // open: gt, lt
  Comparator #(.width(6)) comparator_33 (.a(Instruction[5:0]), .b(6'b100101), .eq(comparator_33_eq));  // open: gt, lt
  Comparator #(.width(6)) comparator_34 (.a(Instruction[5:0]), .b(6'b100111), .eq(comparator_34_eq));  // open: gt, lt
  Comparator #(.width(6)) comparator_35 (.a(Instruction[5:0]), .b(6'b101000), .eq(comparator_35_eq));  // open: gt, lt
  Comparator #(.width(6)) comparator_36 (.a(Instruction[5:0]), .b(6'b001000), .eq(comparator_36_eq));  // open: gt, lt
  Comparator #(.width(6)) comparator_37 (.a(Instruction[5:0]), .b(6'b010000), .eq(comparator_37_eq));  // open: gt, lt
  Comparator #(.width(6)) comparator_38 (.a(Instruction[5:0]), .b(6'b010010), .eq(comparator_38_eq));  // open: gt, lt
  and and_7 (NOP, _000000, comparator_23_eq);
  and and_8 (ADD, _000000, comparator_24_eq);
  and and_9 (SUB, _000000, comparator_25_eq);
  and and_10 (MULT, _000000, comparator_26_eq);
  and and_11 (MULU, _000000, comparator_27_eq);
  and and_12 (DIV, _000000, comparator_28_eq);
  and and_13 (DIVU, _000000, comparator_29_eq);
  and and_14 (SLT, _000000, comparator_30_eq);
  and and_15 (SLTU, _000000, comparator_31_eq);
  and and_16 (AND, _000000, comparator_32_eq);
  and and_17 (OR, _000000, comparator_33_eq);
  and and_18 (NOR, _000000, comparator_34_eq);
  and and_19 (XOR, _000000, comparator_35_eq);
  and and_20 (JR, _000000, comparator_36_eq);
  and and_21 (MFHI, _000000, comparator_37_eq);
  and and_22 (MFLO, _000000, comparator_38_eq);

  assign Constante = Instruction[15:0];
  assign Destino_Salto = Instruction[25:0];
  assign RD = Instruction[15:11];
  assign RS = Instruction[25:21];
  assign RT = Instruction[20:16];
  assign SLT_2 = SLT;

  // Other names for the same wires on the sheet: FUNC_CODE[5:0] = Instruction[5:0]; X[4:0] = Instruction[10:6];
  //   OP_CODE[5:0] = Instruction[31:26]

  // Notes on the sheet:
  //   INSTRUCTION DECODER
endmodule

module Branch_Control (
  input  BEQ,
  input  BNE,
  input  BLEZ,
  input  BGTZ,
  input  BLTZ,
  input  JR,
  input  J,
  input  [25:0] DEST,
  input  [31:0] RS,
  input  [31:0] RT,
  input  [31:0] PC,
  input  [15:0] CONST,
  output [31:0] BC_OUT
);

  wire and_1_out, and_2_out, and_3_out, and_4_out, and_5_out, comparator_2_eq, or_1_out, RS__0, RS___0,
       RS____RT;
  wire [1:0] or_2_out;
  wire [13:0] bit_extender_1_out;
  wire [31:0] PC_4, PC_4_Const_4;

  Adder #(.width(32)) adder_1 (.a(PC), .b(32'h4), .out(PC_4));  // open: cin, cout
  assign bit_extender_1_out = {{13{CONST[15]}}, CONST[15]};  // Bit_Extender bit_extender_1
  Adder #(.width(32)) adder_2 (
    .a(PC_4), .b({bit_extender_1_out, CONST, 2'b00}), .out(PC_4_Const_4));  // open: cin, cout
  and and_1 (and_1_out, BEQ, RS____RT);
  and and_2 (and_2_out, ~RS____RT, BNE);  // AND_Gate
  and and_3 (and_3_out, BLEZ, RS___0);
  and and_4 (and_4_out, ~RS___0, BGTZ);  // AND_Gate
  and and_5 (and_5_out, BLTZ, RS__0);
  Comparator #(.width(32)) comparator_1 (.a(RS), .b(RT), .eq(RS____RT));  // open: gt, lt
  or or_1 (or_1_out, and_1_out, and_2_out, and_3_out, and_4_out, and_5_out);
  or or_2 (or_2_out[0], or_1_out, JR);
  or or_3 (or_2_out[1], J, JR);
  Comparator #(.width(32)) comparator_2 (.a(RS), .b({32{1'b0}}), .eq(comparator_2_eq), .lt(RS__0));  // open: gt
  or or_4 (RS___0, comparator_2_eq, RS__0);
  Multiplexer #(.select(2), .width(32), .enable("false")) multiplexer_1 (
    .in0(PC_4), .in1(PC_4_Const_4), .in2({PC[31:28], DEST, 2'b00}), .in3(RS), .out(BC_OUT), .sel(or_2_out));

  // Other names for the same wires on the sheet: Jmp[31:2] = {PC[31:28], DEST}

  // Notes on the sheet:
  //   Branch Control
endmodule

module Unsigned_Multiplier (
  input  [31:0] A,
  input  [31:0] B,
  output [31:0] HighOutput,
  output [31:0] LowOutput
);

  wire [31:0] adder_1_out, multiplexer_1_out, multiplexer_2_out, multiplier_1_cout;

  Multiplexer #(.width(32), .enable("false")) multiplexer_1 (
    .in0({32{1'b0}}), .in1(A), .out(multiplexer_1_out), .sel(B[31]));
  Multiplexer #(.width(32), .enable("false")) multiplexer_2 (
    .in0({32{1'b0}}), .in1(B), .out(multiplexer_2_out), .sel(A[31]));
  Multiplier #(.width(32)) multiplier_1 (.a(A), .b(B), .out(LowOutput), .cout(multiplier_1_cout));  // open: cin
  Adder #(.width(32)) adder_1 (.a(multiplexer_1_out), .b(multiplexer_2_out), .out(adder_1_out));  // open: cin, cout
  // Probe on LowOutput
  // Probe on LowOutput
  Adder #(.width(32)) adder_2 (.a(multiplier_1_cout), .b(adder_1_out), .out(HighOutput));  // open: cin, cout

  // Notes on the sheet:
  //   UNSIGNED MULTIPLIER
endmodule

module Signed_Divider (
  input  [31:0] A,
  input  [31:0] B,
  output [31:0] HighOutput,
  output [31:0] LowOutput
);

  wire xor_1_out;
  wire [31:0] divider_1_out, multiplexer_1_out, multiplexer_2_out, negator_1_out, negator_2_out,
       negator_3_out;

  Multiplexer #(.width(32), .enable("false")) multiplexer_1 (
    .in0(A), .in1(negator_1_out), .out(multiplexer_1_out), .sel(A[31]));
  Negator #(.width(32)) negator_1 (.in(A), .out(negator_1_out));
  Multiplexer #(.width(32), .enable("false")) multiplexer_2 (
    .in0(B), .in1(negator_2_out), .out(multiplexer_2_out), .sel(B[31]));
  Negator #(.width(32)) negator_2 (.in(B), .out(negator_2_out));
  Divider #(.width(32)) divider_1 (
    .a(multiplexer_1_out), .b(multiplexer_2_out), .out(divider_1_out), .rem(HighOutput));  // open: upper
  xor xor_1 (xor_1_out, A[31], B[31]);
  Negator #(.width(32)) negator_3 (.in(divider_1_out), .out(negator_3_out));
  // Probe on LowOutput
  Multiplexer #(.width(32), .enable("false")) multiplexer_3 (
    .in0(divider_1_out), .in1(negator_3_out), .out(LowOutput), .sel(xor_1_out));
  // Probe on HighOutput

  // Notes on the sheet:
  //   SIGNED DIVIDER
endmodule

module Memory_Address (
  input  [31:0] ALU,
  input  [31:0] PC,
  input  [31:0] SP,
  input  POP,
  input  PUSH,
  input  LW,
  input  SW,
  input  PC_ADDRESS,
  output [31:0] MEMORY
);

  wire [1:0] or_2_out;
  wire [31:0] multiplexer_1_out, subtractor_1_out;

  Subtractor #(.width(32)) subtractor_1 (.a(SP), .b(32'h4), .out(subtractor_1_out));  // open: bin, bout
  Multiplexer #(.width(32), .enable("false")) multiplexer_1 (
    .in0(SP), .in1(subtractor_1_out), .out(multiplexer_1_out), .sel(PUSH));
  or or_1 (or_2_out[1], PUSH, POP, PC_ADDRESS);
  Multiplexer #(.select(2), .width(32), .enable("false")) multiplexer_2 (
    .in0(PC), .in1(ALU), .in2(multiplexer_1_out), .in3(PC), .out(MEMORY), .sel(or_2_out));
  or or_2 (or_2_out[0], PC_ADDRESS, LW, SW);

  // Notes on the sheet:
  //   Memory Address
endmodule

module Timer (
  input  [3:0] TIME,
  input  START,
  input  CLK,
  input  RESET,
  output OUT
);

  wire [3:0] counter_1_q;

  Counter #(.width(4), .max('hf)) counter_1 (
    .count(START), .Q(counter_1_q), .clk(CLK), .clr(RESET));  // open: load, D, carry
  Comparator #(.width(4)) comparator_1 (.a(TIME), .b(counter_1_q), .eq(OUT));  // open: gt, lt

  // Notes on the sheet:
  //   Timer
endmodule

module LittleEndian_BigEndian (
  input  [31:0] INSTRUCTION,
  output [31:0] OUTPUT
);


  assign OUTPUT = {INSTRUCTION[7:0], INSTRUCTION[15:8], INSTRUCTION[23:16], INSTRUCTION[31:24]};
endmodule

module Write_to_RAM (
  input  [31:0] MEMORY,
  input  [31:0] VALUE,
  output [3:0] MASK,
  output [15:0] ADDRESS,
  output [31:0] INPUT0,
  output [31:0] INPUT1,
  output [31:0] INPUT2,
  output [31:0] INPUT3
);

  wire [31:0] littleendian_bigendian_1_output;

  Demultiplexer #(.select(2), .enable("false")) demultiplexer_1 (
    .out0(MASK[0]), .out1(MASK[1]), .out2(MASK[2]), .out3(MASK[3]), .in(1'b1), .sel(MEMORY[3:2]));
  LittleEndian_BigEndian littleendian_bigendian_1 (.INSTRUCTION(VALUE), .OUTPUT(littleendian_bigendian_1_output));
  Demultiplexer #(.select(2), .width(32), .enable("false")) demultiplexer_2 (
    .out0(INPUT0), .out1(INPUT1), .out2(INPUT2), .out3(INPUT3), .in(littleendian_bigendian_1_output),
    .sel(MEMORY[3:2]));

  assign ADDRESS = MEMORY[19:4];

  // Other names for the same wires on the sheet: SELECTOR[1:0] = MEMORY[3:2]
endmodule

module Read_from_RAM (
  input  [31:0] BANK0,
  input  [31:0] BANK1,
  input  [31:0] BANK2,
  input  [31:0] BANK3,
  input  [31:0] MEMORY,
  output [31:0] RAM_DATA
);

  wire [31:0] multiplexer_1_out;

  Multiplexer #(.select(2), .width(32), .enable("false")) multiplexer_1 (
    .in0(BANK0), .in1(BANK1), .in2(BANK2), .in3(BANK3), .out(multiplexer_1_out), .sel(MEMORY[3:2]));
  LittleEndian_BigEndian littleendian_bigendian_1 (.INSTRUCTION(multiplexer_1_out), .OUTPUT(RAM_DATA));

  // Other names for the same wires on the sheet: SELECTOR[1:0] = MEMORY[3:2]
endmodule
